# Fritzing sketch V1 (saved by Fritzing 1.0.7)
breadboards: 1

parts:
  LED1 = LED - 5mm [color="Blue (505nm)" current=30mA package="5 mm [THT]"]
  LED2 = LED - 5mm [color="Red (633nm)" current=0.030A package="5 mm [THT]"]
  R1 = Resistor [tolerance=±5% power=0.25W resistance=10 package=THT]
  R2 = Resistor [tolerance=±5% power=0.25W resistance=47 package=THT]
  A1 = XIAO ESP32C3-tht
  LED3 = LED - 5mm [color="Green (555nm)" current=30mA package="5 mm [THT]"]
  LED4 = LED - 5mm [color="Yellow (574nm)" current=0.030A package="5 mm [THT]"]
  R4 = Resistor [tolerance=±5% power=0.25W resistance=47 package=THT]
  R5 = Resistor [tolerance=±5% power=0.25W resistance=47 package=THT]

nets:
  N1: LED1.cathode, R1.Pin_0
  N2: LED1.anode, A1.Pin_10
  N3: LED2.cathode, R2.Pin_0
  N4: LED2.anode, A1.Pin_9
  N5: R1.Pin_1, R2.Pin_1, A1.Pin_2, A1.Pin_21, LED3.cathode, R4.Pin_0, R4.Pin_1
  N6: A1.Pin_11, LED4.anode
  N7: A1.Pin_12, LED3.anode
  N8: LED4.cathode, R5.Pin_0

custom parts:
  XIAO ESP32C3-tht: Seeed Studio XIAO ESP32C3 adopts new RISC-V architecture, supporting both Wi-Fi and BLE wireless connectivities.
