# Fritzing sketch V2 (saved by Fritzing 1.0.7)
breadboards: 1

parts:
  LED1 = LED - 5mm [color="Blue (525nm)" current=0.030A package="5 mm [THT]"]
  LED2 = LED - 5mm [color="Red (633nm)" current=0.030A package="5 mm [THT]"]
  LED3 = LED - 5mm [color="Yellow (592nm)" current=30mA package="5 mm [THT]"]
  LED4 = LED - 5mm [color="Green (560nm)" current=0.030A package="5 mm [THT]"]
  A2 = XIAO ESP32C3-tht
  R1 = Resistor [tolerance=±5% power=0.25W resistance=220 package=THT]
  R2 = Resistor [tolerance=±5% power=0.25W resistance=220 package=THT]
  R3 = Resistor [tolerance=±5% power=0.25W resistance=220 package=THT]
  R4 = Resistor [tolerance=±5% power=0.25W resistance=220 package=THT]

nets:
  N1: LED1.cathode, R1.Pin_1
  N2: LED1.anode, A2.Pin_12
  N3: LED2.cathode, R2.Pin_1
  N4: LED2.anode, A2.Pin_11
  N5: LED3.cathode, R3.Pin_1
  N6: LED3.anode, A2.Pin_10
  N7: LED4.cathode, R4.Pin_1
  N8: LED4.anode, A2.Pin_9
  N9: A2.Pin_2, A2.Pin_21, R1.Pin_0, R2.Pin_0, R3.Pin_0, R4.Pin_0

custom parts:
  XIAO ESP32C3-tht: Seeed Studio XIAO ESP32C3 adopts new RISC-V architecture, supporting both Wi-Fi and BLE wireless connectivities.
